// Logisim project CPU-MK3.circ as structural Verilog
module RAM (
  input  Incr_SP,
  input  Decr_SP,
  input  SET_SP,
  input  SP_Low_High_byte,
  input  PUSH,
  input  POP,
  input  HEAD,
  input  [15:0] Address_IN,
  input  [7:0] Data_IN,
  input  Write_Instr,
  input  Write_RAM,
  input  Output,
  input  Clear,
  output [7:0] INST,
  output [7:0] DATA
);

  wire clock_1_out, not_1_out, or_4_out;
  wire [7:0] demultiplexer_1_out0, demultiplexer_1_out1;
  wire [15:0] bit_extender_1_out, controlled_buffer_4_out, controlled_buffer_5_out, or_1_out, or_2_out,
       or_3_out, pull_resistor_1_node, pull_resistor_2_node, pull_resistor_3_node, shifter_1_out,
       Stack_Size_q, subtractor_1_out;

  Demultiplexer #(.width(8), .disabled(0), .enable("false")) demultiplexer_1 (
    .out0(demultiplexer_1_out0), .out1(demultiplexer_1_out1), .in(Data_IN), .sel(Write_Instr));
  assign bit_extender_1_out = {{8{1'b0}}, Data_IN};  // Bit_Extender bit_extender_1
  not not_1 (not_1_out, SP_Low_High_byte);
  Pull_Resistor pull_resistor_1 (.node(pull_resistor_1_node));
  assign pull_resistor_1_node = PUSH ? Stack_Size_q : 16'bz;  // Controlled_Buffer controlled_buffer_1
  assign or_1_out = pull_resistor_1_node | Address_IN;  // OR_Gate or_1, 16 bits wide
  Pull_Resistor pull_resistor_2 (.node(pull_resistor_2_node));
  assign pull_resistor_2_node = not_1_out ? bit_extender_1_out : 16'bz;  // Controlled_Buffer controlled_buffer_2
  Pull_Resistor pull_resistor_3 (.node(pull_resistor_3_node));
  assign pull_resistor_3_node = SP_Low_High_byte ? bit_extender_1_out : 16'bz;  // Controlled_Buffer controlled_buffer_3
  Clock clock_1 (.out(clock_1_out));
  assign or_2_out = {demultiplexer_1_out0, INST} | {DATA, demultiplexer_1_out1};  // OR_Gate or_2, 16 bits wide
  assign controlled_buffer_4_out = Decr_SP ? subtractor_1_out : 16'bz;  // Controlled_Buffer controlled_buffer_4
  Pull_Resistor pull_resistor_4 (.node(controlled_buffer_4_out));
  assign controlled_buffer_5_out = SET_SP ? Stack_Size_q : 16'bz;  // Controlled_Buffer controlled_buffer_5
  Pull_Resistor pull_resistor_5 (.node(controlled_buffer_5_out));
  assign or_3_out = controlled_buffer_5_out | controlled_buffer_4_out | pull_resistor_2_node | shifter_1_out;  // OR_Gate or_3, 16 bits wide
  Shifter #(.width(16)) shifter_1 (.in(pull_resistor_3_node), .\dist (4'b1000), .out(shifter_1_out));
  or or_4 (or_4_out, SET_SP, Decr_SP);
  RAM_part #(.addrWidth(16), .dataWidth(16), .bus("separate")) ram_1 (
    .addr(or_1_out), .din(or_2_out), .data({DATA, INST}), .str(Write_RAM), .clk(clock_1_out), .ld(Output),
    .clr(Clear));  // open: sel
  Subtractor #(.width(16)) subtractor_1 (.a(Stack_Size_q), .b(16'h1), .out(subtractor_1_out));  // open: bin, bout
  Counter #(.width(16), .max('hffff), .ongoal("stay")) Stack_Size (
    .load(or_4_out), .D(or_3_out), .count(Incr_SP), .Q(Stack_Size_q), .clk(clock_1_out));  // open: carry, clr
  Pull_Resistor pull_resistor_6 (.node({DATA, INST}));
endmodule

module Register_Bank (
  input  [7:0] in_1,
  input  [2:0] in_2,
  input  [2:0] in_3,
  input  in_4,
  input  in_5,
  input  in_6,
  input  in_7,
  output [7:0] out_8
);

  wire clock_1_out, decoder_1_out0, decoder_1_out1, decoder_1_out2, decoder_1_out3, decoder_1_out4,
       decoder_1_out5, decoder_1_out6, decoder_1_out7, decoder_2_out0, decoder_2_out1, decoder_2_out2,
       decoder_2_out3, decoder_2_out4, decoder_2_out5, decoder_2_out6, decoder_2_out7, not_1_out, not_2_out,
       or_3_out, or_5_out;
  wire [2:0] controlled_buffer_3_out, controlled_buffer_4_out, controlled_buffer_5_out,
       controlled_buffer_6_out, or_2_out, or_4_out;
  wire [7:0] controlled_buffer_2_out, or_1_out, pull_resistor_1_node, register_1_q, register_2_q,
       register_3_q, register_4_q, register_5_q, register_6_q, register_7_q, register_8_q;

  Pull_Resistor pull_resistor_1 (.node(pull_resistor_1_node));
  assign pull_resistor_1_node = not_1_out ? in_1 : 8'bz;  // Controlled_Buffer controlled_buffer_1
  assign controlled_buffer_2_out = in_6 ? out_8 : 8'bz;  // Controlled_Buffer controlled_buffer_2
  Pull_Resistor pull_resistor_2 (.node(controlled_buffer_2_out));
  assign or_1_out = controlled_buffer_2_out | pull_resistor_1_node;  // OR_Gate or_1, 8 bits wide
  not not_1 (not_1_out, in_6);
  assign controlled_buffer_3_out = not_2_out ? in_2 : 3'bz;  // Controlled_Buffer controlled_buffer_3
  Pull_Resistor pull_resistor_3 (.node(controlled_buffer_3_out));
  assign controlled_buffer_4_out = in_6 ? in_3 : 3'bz;  // Controlled_Buffer controlled_buffer_4
  Pull_Resistor pull_resistor_4 (.node(controlled_buffer_4_out));
  assign or_2_out = controlled_buffer_3_out | controlled_buffer_4_out;  // OR_Gate or_2, 3 bits wide
  Decoder #(.select(3), .disabled(0)) decoder_1 (
    .out0(decoder_1_out0), .out1(decoder_1_out1), .out2(decoder_1_out2), .out3(decoder_1_out3),
    .out4(decoder_1_out4), .out5(decoder_1_out5), .out6(decoder_1_out6), .out7(decoder_1_out7),
    .sel(or_2_out), .en(or_3_out));
  or or_3 (or_3_out, in_4, in_6);
  Decoder #(.select(3), .disabled(0)) decoder_2 (
    .out0(decoder_2_out0), .out1(decoder_2_out1), .out2(decoder_2_out2), .out3(decoder_2_out3),
    .out4(decoder_2_out4), .out5(decoder_2_out5), .out6(decoder_2_out6), .out7(decoder_2_out7), .sel(in_2),
    .en(in_5));
  Clock clock_1 (.out(clock_1_out));
  Register register_1 (.D(or_1_out), .en(decoder_1_out0), .Q(register_1_q), .clk(clock_1_out), .clr(decoder_2_out0));
  Register register_2 (.D(or_1_out), .en(decoder_1_out4), .Q(register_2_q), .clk(clock_1_out), .clr(decoder_2_out4));
  Register register_3 (.D(or_1_out), .en(decoder_1_out1), .Q(register_3_q), .clk(clock_1_out), .clr(decoder_2_out1));
  Register register_4 (.D(or_1_out), .en(decoder_1_out5), .Q(register_4_q), .clk(clock_1_out), .clr(decoder_2_out5));
  Register register_5 (.D(or_1_out), .en(decoder_1_out2), .Q(register_5_q), .clk(clock_1_out), .clr(decoder_2_out2));
  Register register_6 (.D(or_1_out), .en(decoder_1_out6), .Q(register_6_q), .clk(clock_1_out), .clr(decoder_2_out6));
  not not_2 (not_2_out, in_6);
  assign controlled_buffer_5_out = in_6 ? in_2 : 3'bz;  // Controlled_Buffer controlled_buffer_5
  Pull_Resistor pull_resistor_5 (.node(controlled_buffer_5_out));
  assign controlled_buffer_6_out = not_2_out ? in_3 : 3'bz;  // Controlled_Buffer controlled_buffer_6
  Register register_7 (.D(or_1_out), .en(decoder_1_out3), .Q(register_7_q), .clk(clock_1_out), .clr(decoder_2_out3));
  Register register_8 (.D(or_1_out), .en(decoder_1_out7), .Q(register_8_q), .clk(clock_1_out), .clr(decoder_2_out7));
  assign or_4_out = controlled_buffer_5_out | controlled_buffer_6_out;  // OR_Gate or_4, 3 bits wide
  Pull_Resistor pull_resistor_6 (.node(controlled_buffer_6_out));
  Multiplexer #(.select(3), .width(8), .disabled(0)) multiplexer_1 (
    .in0(register_1_q), .in1(register_3_q), .in2(register_5_q), .in3(register_7_q), .in4(register_2_q),
    .in5(register_4_q), .in6(register_6_q), .in7(register_8_q), .out(out_8), .sel(or_4_out), .en(or_5_out));
  or or_5 (or_5_out, in_6, in_7);
endmodule
